# Fritzing sketch Eksamen_2017 (saved by Fritzing 0.9.3b)
breadboards: 1

parts:
  TFT1 = 1.8" TFT Display with uSD
  Part1 = Arduino Uno (Rev3) - ICSP
  ZS-042_RTC1 = ZS-042 RTC Module
  Part2 = Soil Moisture Sensor
  DHT1 = DHT11 Humitidy and Temperature Sensor
  J1 = Piezo Speaker
  R1 = Resistor [tolerance=±5% resistance=220 package="2010 [SMD]"]
  R2 = Resistor [tolerance=±5% resistance=220 package="2512 [SMD]"]
  R3 = PHOTOCELL [package=photocell]
  LED1 = smd LED [color="Red (633nm)" package="0805 [SMD]"]
  LED2 = smd LED [color="Red (633nm)" package="0805 [SMD]"]
  LED3 = smd LED [color="Red (633nm)" package="0805 [SMD]"]
  LED4 = smd LED [color="Red (633nm)" package="0805 [SMD]"]
  LED5 = smd LED [color="Green (555nm)" package="1206 [SMD]"]
  R4 = Resistor [tolerance=±5% resistance=220 package="0805 [SMD]"]  # not connected
  R5 = Resistor [tolerance=±5% resistance=220 package="0805 [SMD]"]
  R6 = Resistor [tolerance=±5% resistance=220 package="0805 [SMD]"]
  R7 = Resistor [tolerance=±5% resistance=220 package="0805 [SMD]"]
  R8 = Resistor [tolerance=±5% resistance=220 package="0805 [SMD]"]

nets:
  GND: TFT1.BL, Part1.GND, ZS-042_RTC1.GND, Part2.GND, DHT1.GND, J1.pin1, R1.Pin_1, R2.Pin_1
  VCC: TFT1.MISO, Part1.5V, ZS-042_RTC1.VCC, Part2.VCC, DHT1.VDD, R3.P$1
  N1: TFT1.SCK, Part1.D8
  N2: TFT1.MOSI, Part1.D9_PWM
  N3: TFT1.SDCS, Part1.D10_PWM/SS
  N4: TFT1.RST, Part1.D13/SCK
  N5: TFT1.VCC, Part1.D11_PWM/MOSI
  N6: Part1.A0, R2.Pin_0, R3.P$2
  N7: Part1.A4/SDA, ZS-042_RTC1.SDA
  N8: Part1.A5/SCL, ZS-042_RTC1.SCL
  N9: Part1.ICSP_MISO, Part1.D12/MISO, LED1.cathode
  N10: Part1.D2, DHT1.DATA
  N11: Part1.D3_PWM, J1.pin2
  N12: Part1.D4, LED2.cathode
  N13: Part1.D5_PWM, LED5.cathode
  N14: Part1.D6_PWM, LED4.cathode
  N15: Part1.D7, LED3.cathode
  N16: LED2.anode, R5.Pin_0
  N17: LED3.anode, R6.Pin_0
  N18: LED4.anode, R7.Pin_0
  N19: LED5.anode, R8.Pin_0

custom parts:
  1.8" TFT Display with uSD: 1.8" TFT Display with SPI control and MicroSD card
  DHT11 Humitidy and Temperature Sensor: DHT11 Humidity and Temperature Sensor
